# Fritzing sketch BreadBord (saved by Fritzing 0.9.3b)
breadboards: 1

parts:
  IC2 = ULN2003A [package="SO16 [SMD]"]
  元件2 = Arduino Uno (Rev3) - ICSP
  LED2 = RGB LED (com. cathode, rgb) [package="5 mm [THT]"]
  J3 = Basic Servo
  R5 = Resistor [tolerance=±5% resistance=220 package="1206 [SMD]"]
  R6 = Resistor [tolerance=±5% resistance=220 package="1206 [SMD]"]
  R7 = Resistor [tolerance=±5% resistance=220 package="1206 [SMD]"]
  R8 = Resistor [tolerance=±5% resistance=220 package="1206 [SMD]"]
  S4 = Square Pushbutton
  S5 = Toggle Switch [package=THT]
  S6 = Toggle Switch [package=THT]
  J4 = Basic Servo
  BAT1 = BC9VPC [package=bc9vpc]
  S7 = Square Pushbutton
  R9 = Resistor [tolerance=±5% resistance=220 package=THT]
  R10 = Resistor [tolerance=±5% resistance=220 package=THT]

nets:
  N1: IC2.In_1, 元件2.D7
  N2: IC2.In_2, 元件2.D2
  N3: IC2.0V, R5.Pin_0, R6.Pin_0, R7.Pin_0, R8.Pin_0, S4.leg1, S7.leg1
  N4: IC2.Out_2, J4.gnd
  N5: IC2.Out_1, J3.gnd
  N6: 元件2.D8, LED2.red_anode
  N7: 元件2.D9_PWM, LED2.blue_anode
  N8: 元件2.D10_PWM/SS, LED2.green_anode
  N9: 元件2.D5_PWM, S7.leg0, R9.Pin_1
  N10: 元件2.D6_PWM, S4.leg0, R10.Pin_0
  N11: 元件2.5V, S5.L2, S6.L2
  N12: 元件2.GND, BAT1.V-
  N13: LED2.common_cathode, R5.Pin_1
  VCC: J3.vcc, J4.vcc, BAT1.V+, R9.Pin_0, R10.Pin_1
  N14: R7.Pin_1, S5.COM
  N15: R8.Pin_1, S6.COM
